# Fritzing sketch ForexTracker (saved by Fritzing 0.9.3b)
breadboards: 1

parts:
  S2 = Pushbutton [package="[THT]"]
  S1 = Pushbutton [package="[THT]"]
  R1 = Resistor [tolerance=±5% resistance=10k package="2512 [SMD]"]
  NODEMCU = NodeMCU V1.0
  S4 = Pushbutton [package="[THT]"]
  R2 = Resistor [tolerance=±5% resistance=10k package="2512 [SMD]"]
  S3 = Pushbutton [package="[THT]"]
  OLED = OLED 0.96" 128x64 I2C SSD1306
  R3 = Resistor [tolerance=±5% resistance=10k package="2512 [SMD]"]
  LED1 = RGB LED (com. cathode, rgb) [package="5 mm [THT]"]

nets:
  3V3: S2.Pin_1, S2.Pin_2, NODEMCU.3V3, S4.Pin_1, S4.Pin_2, S3.Pin_1, S3.Pin_2, OLED.VCC
  N1: S2.Pin_3, S2.Pin_4, R1.Pin_1, NODEMCU.D6
  GND: S1.Pin_1, S1.Pin_2, R1.Pin_0, NODEMCU.GND, R2.Pin_0, OLED.GND, R3.Pin_0, LED1.common_cathode
  N2: S1.Pin_3, S1.Pin_4, NODEMCU.D5
  N3: NODEMCU.D0, LED1.red_anode
  N4: NODEMCU.D1, OLED.SCL
  N5: NODEMCU.D2, OLED.SCA
  N6: NODEMCU.D3, LED1.green_anode
  N7: NODEMCU.D4, LED1.blue_anode
  N8: NODEMCU.D7, R2.Pin_1, S3.Pin_3, S3.Pin_4
  N9: NODEMCU.D8, S4.Pin_3, S4.Pin_4, R3.Pin_1

custom parts:
  NodeMCU V1.0: ESP8266 based NodeMCU
